# Fritzing sketch fan_ctrl (saved by Fritzing 0.9.10b)
breadboards: 1

parts:
  Pico_H1 = Raspberry Pi Pico H
  R1 = Temperature Sensor (Thermistor) [thermistor_type=NTC package=THT]
  R2 = Resistor [tolerance=±5% power=0.25 resistance=10k package=THT]
  U1 = RELAY [part_number=jzc-11f package=relay-jzc]
  LED1 = smd LED [color="Blue (430nm)" package="0603 [SMD]"]

nets:
  N1: Pico_H1.GND, R1.pin_1, U1.COIL1, LED1.anode
  N2: Pico_H1.3V3, R2.Pin_1
  N3: Pico_H1.GP28_A2, R1.pin_0, R2.Pin_0
  N4: Pico_H1.GP6, U1.MAIN, LED1.cathode

custom parts:
  Raspberry Pi Pico H: Raspberry Pi Pico H. Based around the RP2040 microcontroller the Pico H is a low cost microcontroller device bringing Raspberry Pi quality, cost, and easy of use to the microcontroller space.
